# Fritzing sketch mrhicks46-rev2 (saved by Fritzing 0.7.7b)
breadboards: 1

parts:
  microSD1 = MicroSD Breakout
  Nano1 = Arduino Nano v3.0

nets:
  N1: microSD1.CS, Nano1.D10
  N2: microSD1.DI, Nano1.D11
  N3: microSD1.DO, Nano1.D12
  N4: microSD1.CLK, Nano1.D13
  GND: microSD1.GND, Nano1.GND
  5V: microSD1.5V, Nano1.+5V

custom parts:
  MicroSD Breakout: 5V-ready microSD Breakout with Level Shifter
