# Fritzing sketch mrhicks46 (saved by Fritzing 0.7.11b)
breadboards: 1

parts:
  Arduino_Ethernet_Shield1 = Arduino Ethernet Shield
  RTC = Real Time Clock Module - DS1307 RTC Breakout Board
  GPS1 = Adafruit Ultimate GPS Breakout
  CAMERA1 = TTL Serial JPEG Camera
  PUSH = Round Pushbutton
  DS1 = DS18B20 1-Wire Temperature Sensor [part_number=DS18B20]
  R1 = Resistor [tolerance=±5% resistance=220 package=THT]
  LED1 = RGB LED - (4 legs) [package="5 mm [THT]"]
  R2 = Resistor [tolerance=±5% resistance=220 package=THT]
  R3 = Resistor [tolerance=±5% resistance=220 package=THT]

nets (from the pcb view):
  N1: Arduino_Ethernet_Shield1.D9, CAMERA1.TX
  N2: Arduino_Ethernet_Shield1.D8, PUSH.leg0
  N3: Arduino_Ethernet_Shield1.D6, R3.Pin_0
  N4: Arduino_Ethernet_Shield1.D5, R1.Pin_0
  N5: Arduino_Ethernet_Shield1.D3, R2.Pin_0
  N6: Arduino_Ethernet_Shield1.D1TX, GPS1.RX
  N7: Arduino_Ethernet_Shield1.D0RX, GPS1.TX
  5V: Arduino_Ethernet_Shield1.+5V, RTC.5V, GPS1.VIN, CAMERA1.5V, PUSH.leg1, DS1.VDD, LED1.common_anode
  GND: Arduino_Ethernet_Shield1.GND, RTC.GND, GPS1.GND, CAMERA1.GND, DS1.GND
  N8: Arduino_Ethernet_Shield1.A0, DS1.DQ
  N9: R1.Pin_1, LED1.green_cathode
  N10: LED1.red_cathode, R2.Pin_1
  N11: LED1.blue_cathode, R3.Pin_1

notes:
  RTC to save dateTime
  Camera TTL
  GPS Unit
  Temperature
  Sensor
  Push button
  to take a snapshot (picture & data)
  RGB Led

custom parts:
  TTL Serial JPEG Camera: TTL Serial JPEG Camera with NTSC Out
